// Logisim project Assignment_1_Digitalelectronics_circuit.circ as structural Verilog: 1 circuit, main circuit main
module main (
  input  A,
  input  in_2,
  input  in_3,
  input  D,
  input  B,
  output out_6,
  output out_7
);

  wire and_1_out, and_2_out, and_3_out, and_4_out, and_5_out, and_6_out, and_7_out, and_8_out, not_1_out,
       not_2_out, not_3_out, not_4_out;

  not not_1 (not_1_out, A);
  not not_2 (not_2_out, in_2);
  not not_3 (not_3_out, in_3);
  not not_4 (not_4_out, D);
  not not_5 (out_7, B);
  and and_1 (and_1_out, not_1_out, not_2_out, not_3_out, not_4_out);
  and and_2 (and_2_out, not_1_out, not_2_out, not_3_out, D);
  and and_3 (and_3_out, not_1_out, not_2_out, in_3, not_4_out);
  and and_4 (and_4_out, not_1_out, not_2_out, in_3, D);
  and and_5 (and_5_out, A, not_2_out, not_3_out, not_4_out);
  and and_6 (and_6_out, A, not_2_out, not_3_out, D);
  and and_7 (and_7_out, A, not_2_out, in_3, not_4_out);
  and and_8 (and_8_out, A, not_2_out, in_3, D);
  or or_1 (out_6, and_1_out, and_2_out, and_3_out, and_4_out, and_5_out, and_6_out, and_7_out, and_8_out);

  // Notes on the sheet:
  //   B
  //   C
  //   Assignment 1 Digital Electronics( Simplified circuit)
  //   Ritam Maity_2F_404
  //   Assignment 1 Digital Electronics( Original circuit)
endmodule
