// Logisim project Assignment_2_Digitalelectronics_circuit.circ as structural Verilog: 1 circuit, main circuit main
module main (
  input  D,
  input  W,
  output A
);

  or or_1 (A, D, W);

  // Notes on the sheet:
  //   Assignment 2 Digital Electronics
  //   Ritam Maity_2F_404
endmodule
