// Logisim project Assignment_3_Digitalelectronis_Circuit.circ as structural Verilog: 1 circuit, main circuit main
module main (
  input  p,
  output G,
  output Y,
  output R,
  output Ped
);

  wire and_1_out, and_2_out, clock_1_out, d_ff_2_q, not_1_out, not_2_out, or_1_out;

  Clock clock_1 (.out(clock_1_out));
  D_Flip_Flop d_ff_1 (.D(and_1_out), .clk(clock_1_out), .Q(R));  // open: Qn, preset, reset
  D_Flip_Flop d_ff_2 (.D(and_2_out), .clk(clock_1_out), .Q(d_ff_2_q));  // open: Qn, preset, reset
  not not_1 (not_1_out, R);
  not not_2 (not_2_out, d_ff_2_q);
  and and_1 (and_1_out, not_1_out, d_ff_2_q);
  or or_1 (or_1_out, not_1_out, p);
  and and_2 (and_2_out, or_1_out, not_2_out);
  and and_3 (G, not_1_out, not_2_out);
  and and_4 (Y, not_1_out, d_ff_2_q);
  and and_5 (Ped, R, d_ff_2_q);

  // Notes on the sheet:
  //   clk
  //   Assignment 3 Digital electronics
  //   Ritam Maity_2F_404
  //   Q1
  //   Q0
  //   D1
  //   D0
endmodule
