// Logisim project Assignment_4_Digitalelectronis_Circuit.circ as structural Verilog: 1 circuit, main circuit main
module main (
  input  A,
  input  B,
  input  Cin,
  input  A_2,
  input  B_2,
  input  Cin_2,
  output Sum,
  output out_8,
  output Sum_2,
  output Cout
);

  wire and_1_out, and_2_out, and_3_out, and_4_out, and_5_out, xor_1_out, xor_2_out;

  xor xor_1 (xor_1_out, A, B);
  xor xor_2 (xor_2_out, A_2, B_2);
  xor xor_3 (Sum, xor_1_out, Cin);
  and and_1 (and_1_out, A, B);
  and and_2 (and_2_out, A, Cin);
  xor xor_4 (Sum_2, xor_2_out, Cin_2);
  and and_3 (and_3_out, A_2, B_2);
  and and_4 (and_4_out, A_2, Cin_2);
  and and_5 (and_5_out, B_2, Cin_2);
  or or_1 (out_8, and_1_out, and_2_out);
  or or_2 (Cout, and_3_out, and_4_out, and_5_out);

  // Notes on the sheet:
  //   Faulty Full Adder Circuit
  //   Corrected Full Adder Circuit
  //   Assignment 4 Digital Electronics 
  //   Ritam Maity_2F_404
  //   Cout (faulty)
endmodule
