// Logisim project Assignment_6_Digitalelectronis_Circuit.circ as structural Verilog: 1 circuit, main circuit main
module main (
  input  in_1,
  input  in_2,
  output out_3,
  output out_4,
  output out_5,
  output out_6,
  output out_7
);

  wire clock_1_out, clock_2_out, clock_3_out;

  Clock clock_1 (.out(clock_1_out));
  Clock clock_2 (.out(clock_2_out));
  Clock clock_3 (.out(clock_3_out));
  Counter #(.max('h3b), .width(6)) counter_1 (.clk(clock_1_out));  // open: clr, load, up, count, D, carry, Q
  D_Flip_Flop d_ff_1 (.D(in_2), .clk(clock_2_out), .Q(out_4));  // open: Qn, preset, reset
  D_Flip_Flop d_ff_2 (.D(in_1), .clk(clock_3_out), .Q(out_3));  // open: Qn, preset, reset
  D_Flip_Flop d_ff_3 (.D(out_4), .clk(clock_2_out), .Q(out_5));  // open: Qn, preset, reset
  D_Flip_Flop d_ff_4 (.D(out_5), .clk(clock_2_out), .Q(out_6));  // open: Qn, preset, reset
  D_Flip_Flop d_ff_5 (.D(out_6), .clk(clock_2_out), .Q(out_7));  // open: Qn, preset, reset

  // Notes on the sheet:
  //   Application 2: Mod-60 Counter
  //   Application 3: Shift Register
  //   Application 1 – D Flip-Flop as 1-Bit Memory
  //   Assignment 6 Digital Electronics
  //   Ritam Maity_2F_404
endmodule
