// Logisim project Assignment_7_Digitalelectronis_Circuit.circ as structural Verilog: 1 circuit, main circuit main
module main (
  input  v,
  output out_2
);

  wire and_1_out, clock_1_out, d_ff_1_q, d_ff_2_q, not_1_out, not_2_out;

  Clock clock_1 (.out(clock_1_out));
  D_Flip_Flop d_ff_1 (.D(and_1_out), .clk(clock_1_out), .Q(d_ff_1_q));  // open: Qn, preset, reset
  and and_1 (and_1_out, not_1_out, not_2_out, d_ff_2_q);
  not not_1 (not_1_out, d_ff_1_q);
  not not_2 (not_2_out, v);
  D_Flip_Flop d_ff_2 (.D(v), .clk(clock_1_out), .Q(d_ff_2_q));  // open: Qn, preset, reset
  or or_1 (out_2, d_ff_1_q, d_ff_2_q);
endmodule
