// Logisim project Assignment_8_Digitalelectronis_Circuit.circ as structural Verilog: 1 circuit, main circuit main
module main (
  input  [3:0] A,
  input  [3:0] B,
  input  M,
  input  Reset,
  input  En,
  input  in_6,
  input  [3:0] one,
  input  Reset_2,
  input  En_2,
  output [3:0] S,
  output [3:0] out_11,
  output out_12,
  output out_13,
  output out_14,
  output out_15
);

  wire clock_1_out;
  wire [3:0] adder_2_out, adder_3_out, multiplexer_2_out, xor_1_out;

  D_Flip_Flop d_ff_1 (.D(adder_2_out[0]), .clk(in_6), .Q(out_12), .reset(Reset_2));  // open: Qn, preset
  D_Flip_Flop d_ff_2 (.D(adder_2_out[1]), .clk(in_6), .Q(out_13), .reset(Reset_2));  // open: Qn, preset
  xor xor_1 (xor_1_out[0], B[0], M);
  xor xor_2 (xor_1_out[1], B[1], M);
  xor xor_3 (xor_1_out[2], B[2], M);
  xor xor_4 (xor_1_out[3], B[3], M);
  D_Flip_Flop d_ff_3 (.D(adder_2_out[2]), .clk(in_6), .Q(out_14), .reset(Reset_2));  // open: Qn, preset
  D_Flip_Flop d_ff_4 (.D(adder_2_out[3]), .clk(in_6), .Q(out_15), .reset(Reset_2));  // open: Qn, preset
  Adder #(.width(4)) adder_1 (.a(A), .b(xor_1_out), .out(S), .cin(M));  // open: cout
  Adder #(.width(4)) adder_2 (.a({out_15, out_14, out_13, out_12}), .b(one), .out(adder_2_out));  // open: cin, cout
  Multiplexer #(.width(4)) multiplexer_1 (
    .in0({out_15, out_14, out_13, out_12}), .in1(adder_2_out), .out(adder_2_out), .sel(En_2));
  Adder #(.width(4)) adder_3 (.a(out_11), .b(4'b0001), .out(adder_3_out));  // open: cin, cout
  Multiplexer #(.width(4)) multiplexer_2 (.in0(out_11), .in1(adder_3_out), .out(multiplexer_2_out), .sel(En));
  Register #(.width(4)) register_1 (.D(multiplexer_2_out), .en(En), .clk(clock_1_out), .Q(out_11), .clr(Reset));
  Clock clock_1 (.out(clock_1_out));

  // Notes on the sheet:
  //   4-bit Mini-ALU
  //   4-bit Program Counter 
  //   FF0
  //   FF1
  //   FF2
  //   FF3
  //   4-bit Program Counter
endmodule
