// Logisim project Assignment_9_Digitalelectronis_Circuit.circ as structural Verilog: 1 circuit, main circuit main
module main (
  input  [3:0] A,
  input  [3:0] B,
  output [3:0] C
);

  Adder #(.width(4)) adder_1 (.a(A), .b(B), .out(C));  // open: cin, cout

  // Notes on the sheet:
  //   Logic Circuit Implementation of Code C = A + B Using a 4-Bit Adder in Logisim Evolution
  //   Assignment 9 Degital Electronics
  //   Ritam Maity_2F_404
endmodule
